// Logisim project 318895877_introduction.circ as structural Verilog: 1 circuit, main circuit comb
module comb (
  input  a,
  input  b,
  input  c,
  output y
);

  wire and_1_out, not_1_out;

  not not_1 (not_1_out, a);
  and and_1 (and_1_out, b, c);
  or or_1 (y, not_1_out, and_1_out);
endmodule
