// Logisim project 318895877_matmul.circ as structural Verilog: 11 circuits, main circuit matmul
module matmul (
  input  [7:0] x_row_0,
  input  [7:0] x_row_1,
  input  [7:0] x_row_2,
  input  [7:0] x_row_3,
  input  [7:0] x_row_4,
  input  [7:0] x_row_5,
  input  [7:0] x_row_6,
  input  [7:0] x_row_7,
  input  [7:0] y_row_0,
  input  [7:0] y_row_1,
  input  [7:0] y_row_2,
  input  [7:0] y_row_3,
  input  [7:0] y_row_4,
  input  [7:0] y_row_5,
  input  [7:0] y_row_6,
  input  [7:0] y_row_7,
  output [7:0] z_row_0,
  output [7:0] z_row_1,
  output [7:0] z_row_2,
  output [7:0] z_row_3,
  output [7:0] z_row_4,
  output [7:0] z_row_5,
  output [7:0] z_row_6,
  output [7:0] z_row_7
);

  wire [7:0] y_col_0, y_col_1, y_col_2, y_col_3, y_col_4, y_col_5, y_col_6, y_col_7;

  matmul_step_2 matmul_step_2_1 (
    .row(x_row_0), .col_0(y_col_0), .col_1(y_col_1), .col_2(y_col_2), .col_3(y_col_3), .col_4(y_col_4),
    .col_5(y_col_5), .col_6(y_col_6), .col_7(y_col_7), .product_row(z_row_0));
  matmul_step_2 matmul_step_2_2 (
    .row(x_row_1), .col_0(y_col_0), .col_1(y_col_1), .col_2(y_col_2), .col_3(y_col_3), .col_4(y_col_4),
    .col_5(y_col_5), .col_6(y_col_6), .col_7(y_col_7), .product_row(z_row_1));
  DotMatrix #(.inputtype("row"), .matrixcols(8), .matrixrows(8)) dotmatrix_1 (
    .row0(x_row_0), .row1(x_row_1), .row2(x_row_2), .row3(x_row_3), .row4(x_row_4), .row5(x_row_5),
    .row6(x_row_6), .row7(x_row_7));
  DotMatrix #(.inputtype("row"), .matrixcols(8), .matrixrows(8)) dotmatrix_2 (
    .row0(y_row_0), .row1(y_row_1), .row2(y_row_2), .row3(y_row_3), .row4(y_row_4), .row5(y_row_5),
    .row6(y_row_6), .row7(y_row_7));
  transpose transpose_1 (
    .row_0(y_row_0), .row_1(y_row_1), .row_2(y_row_2), .row_3(y_row_3), .row_4(y_row_4), .row_5(y_row_5),
    .row_6(y_row_6), .row_7(y_row_7), .column_0(y_col_0), .column_1(y_col_1), .column_2(y_col_2),
    .column_3(y_col_3), .column_4(y_col_4), .column_5(y_col_5), .column_6(y_col_6), .column_7(y_col_7));
  matmul_step_2 matmul_step_2_3 (
    .row(x_row_2), .col_0(y_col_0), .col_1(y_col_1), .col_2(y_col_2), .col_3(y_col_3), .col_4(y_col_4),
    .col_5(y_col_5), .col_6(y_col_6), .col_7(y_col_7), .product_row(z_row_2));
  matmul_step_2 matmul_step_2_4 (
    .row(x_row_3), .col_0(y_col_0), .col_1(y_col_1), .col_2(y_col_2), .col_3(y_col_3), .col_4(y_col_4),
    .col_5(y_col_5), .col_6(y_col_6), .col_7(y_col_7), .product_row(z_row_3));
  DotMatrix #(.inputtype("row"), .matrixcols(8), .matrixrows(8)) dotmatrix_3 (
    .row0(z_row_0), .row1(z_row_1), .row2(z_row_2), .row3(z_row_3), .row4(z_row_4), .row5(z_row_5),
    .row6(z_row_6), .row7(z_row_7));
  matmul_step_2 matmul_step_2_5 (
    .row(x_row_4), .col_0(y_col_0), .col_1(y_col_1), .col_2(y_col_2), .col_3(y_col_3), .col_4(y_col_4),
    .col_5(y_col_5), .col_6(y_col_6), .col_7(y_col_7), .product_row(z_row_4));
  matmul_step_2 matmul_step_2_6 (
    .row(x_row_5), .col_0(y_col_0), .col_1(y_col_1), .col_2(y_col_2), .col_3(y_col_3), .col_4(y_col_4),
    .col_5(y_col_5), .col_6(y_col_6), .col_7(y_col_7), .product_row(z_row_5));
  matmul_step_2 matmul_step_2_7 (
    .row(x_row_6), .col_0(y_col_0), .col_1(y_col_1), .col_2(y_col_2), .col_3(y_col_3), .col_4(y_col_4),
    .col_5(y_col_5), .col_6(y_col_6), .col_7(y_col_7), .product_row(z_row_6));
  matmul_step_2 matmul_step_2_8 (
    .row(x_row_7), .col_0(y_col_0), .col_1(y_col_1), .col_2(y_col_2), .col_3(y_col_3), .col_4(y_col_4),
    .col_5(y_col_5), .col_6(y_col_6), .col_7(y_col_7), .product_row(z_row_7));
endmodule

module transpose (
  input  [7:0] row_0,
  input  [7:0] row_1,
  input  [7:0] row_2,
  input  [7:0] row_3,
  input  [7:0] row_4,
  input  [7:0] row_5,
  input  [7:0] row_6,
  input  [7:0] row_7,
  output [7:0] column_0,
  output [7:0] column_1,
  output [7:0] column_2,
  output [7:0] column_3,
  output [7:0] column_4,
  output [7:0] column_5,
  output [7:0] column_6,
  output [7:0] column_7
);

  extract_col extract_col_1 (
    .in_1(3'b000), .row_0(row_0), .row_1(row_1), .row_2(row_2), .row_3(row_3), .row_4(row_4), .row_5(row_5),
    .row_6(row_6), .row_7(row_7), .b(column_0));
  extract_col extract_col_2 (
    .in_1(3'b100), .row_0(row_0), .row_1(row_1), .row_2(row_2), .row_3(row_3), .row_4(row_4), .row_5(row_5),
    .row_6(row_6), .row_7(row_7), .b(column_4));
  extract_col extract_col_3 (
    .in_1(3'b001), .row_0(row_0), .row_1(row_1), .row_2(row_2), .row_3(row_3), .row_4(row_4), .row_5(row_5),
    .row_6(row_6), .row_7(row_7), .b(column_1));
  extract_col extract_col_4 (
    .in_1(3'b101), .row_0(row_0), .row_1(row_1), .row_2(row_2), .row_3(row_3), .row_4(row_4), .row_5(row_5),
    .row_6(row_6), .row_7(row_7), .b(column_5));
  extract_col extract_col_5 (
    .in_1(3'b010), .row_0(row_0), .row_1(row_1), .row_2(row_2), .row_3(row_3), .row_4(row_4), .row_5(row_5),
    .row_6(row_6), .row_7(row_7), .b(column_2));
  extract_col extract_col_6 (
    .in_1(3'b110), .row_0(row_0), .row_1(row_1), .row_2(row_2), .row_3(row_3), .row_4(row_4), .row_5(row_5),
    .row_6(row_6), .row_7(row_7), .b(column_6));
  extract_col extract_col_7 (
    .in_1(3'b011), .row_0(row_0), .row_1(row_1), .row_2(row_2), .row_3(row_3), .row_4(row_4), .row_5(row_5),
    .row_6(row_6), .row_7(row_7), .b(column_3));
  extract_col extract_col_8 (
    .in_1(3'b111), .row_0(row_0), .row_1(row_1), .row_2(row_2), .row_3(row_3), .row_4(row_4), .row_5(row_5),
    .row_6(row_6), .row_7(row_7), .b(column_7));
endmodule

module extract_col (
  input  [2:0] in_1,
  input  [7:0] row_0,
  input  [7:0] row_1,
  input  [7:0] row_2,
  input  [7:0] row_3,
  input  [7:0] row_4,
  input  [7:0] row_5,
  input  [7:0] row_6,
  input  [7:0] row_7,
  output [7:0] b
);

  wire [2:0] not_1_out, not_2_out, not_3_out, not_4_out, not_5_out, not_6_out, not_7_out, not_8_out;

  BitSelector bitselector_1 (.in(row_0), .out(b[7]), .sel(not_1_out));
  assign not_1_out = ~in_1;  // NOT_Gate not_1, 3 bits wide
  BitSelector bitselector_2 (.in(row_1), .out(b[6]), .sel(not_2_out));
  assign not_2_out = ~in_1;  // NOT_Gate not_2, 3 bits wide
  BitSelector bitselector_3 (.in(row_2), .out(b[5]), .sel(not_3_out));
  assign not_3_out = ~in_1;  // NOT_Gate not_3, 3 bits wide
  BitSelector bitselector_4 (.in(row_3), .out(b[4]), .sel(not_4_out));
  assign not_4_out = ~in_1;  // NOT_Gate not_4, 3 bits wide
  BitSelector bitselector_5 (.in(row_4), .out(b[3]), .sel(not_5_out));
  assign not_5_out = ~in_1;  // NOT_Gate not_5, 3 bits wide
  BitSelector bitselector_6 (.in(row_5), .out(b[2]), .sel(not_6_out));
  assign not_6_out = ~in_1;  // NOT_Gate not_6, 3 bits wide
  BitSelector bitselector_7 (.in(row_6), .out(b[1]), .sel(not_7_out));
  assign not_7_out = ~in_1;  // NOT_Gate not_7, 3 bits wide
  BitSelector bitselector_8 (.in(row_7), .out(b[0]), .sel(not_8_out));
  assign not_8_out = ~in_1;  // NOT_Gate not_8, 3 bits wide

  // Other names for the same wires on the sheet: col[7:0] = b; col_num[2:0] = in_1
endmodule

module matmul_step_1 (
  input  [7:0] row,
  input  [7:0] col,
  output \output 
);

  wire and_1_out, and_2_out, and_3_out, and_4_out, and_5_out, and_6_out, and_7_out, and_8_out, or_1_out,
       or_2_out, or_3_out, or_4_out, or_5_out, or_6_out;

  and and_1 (and_1_out, row[0], col[0]);
  and and_2 (and_2_out, row[1], col[1]);
  and and_3 (and_3_out, row[2], col[2]);
  and and_4 (and_4_out, row[3], col[3]);
  and and_5 (and_5_out, row[4], col[4]);
  and and_6 (and_6_out, row[5], col[5]);
  and and_7 (and_7_out, row[6], col[6]);
  and and_8 (and_8_out, row[7], col[7]);
  or or_1 (or_1_out, and_1_out, and_2_out);
  or or_2 (or_2_out, and_3_out, and_4_out);
  or or_3 (or_3_out, and_5_out, and_6_out);
  or or_4 (or_4_out, and_7_out, and_8_out);
  or or_5 (or_5_out, or_1_out, or_2_out);
  or or_6 (or_6_out, or_3_out, or_4_out);
  or or_7 (\output , or_5_out, or_6_out);

  // Other names for the same wires on the sheet: col_0 = col[0]; col_1 = col[1]; col_2 = col[2]; col_3 = col[3];
  //   col_4 = col[4]; col_5 = col[5]; col_6 = col[6]; col_7 = col[7]; row_0 = row[0]; row_1 = row[1]; row_2 = row[2];
  //   row_3 = row[3]; row_4 = row[4]; row_5 = row[5]; row_6 = row[6]; row_7 = row[7]
endmodule

module matmul_step_2 (
  input  [7:0] row,
  input  [7:0] col_0,
  input  [7:0] col_1,
  input  [7:0] col_2,
  input  [7:0] col_3,
  input  [7:0] col_4,
  input  [7:0] col_5,
  input  [7:0] col_6,
  input  [7:0] col_7,
  output [7:0] product_row
);

  matmul_step_1 matmul_step_1_1 (.row(row), .col(col_0), .\output (product_row[7]));
  matmul_step_1 matmul_step_1_2 (.row(row), .col(col_1), .\output (product_row[6]));
  matmul_step_1 matmul_step_1_3 (.row(row), .col(col_2), .\output (product_row[5]));
  matmul_step_1 matmul_step_1_4 (.row(row), .col(col_3), .\output (product_row[4]));
  matmul_step_1 matmul_step_1_5 (.row(row), .col(col_4), .\output (product_row[3]));
  matmul_step_1 matmul_step_1_6 (.row(row), .col(col_5), .\output (product_row[2]));
  matmul_step_1 matmul_step_1_7 (.row(row), .col(col_6), .\output (product_row[1]));
  matmul_step_1 matmul_step_1_8 (.row(row), .col(col_7), .\output (product_row[0]));

  // Other names for the same wires on the sheet: product_row_0 = product_row[0]; product_row_1 = product_row[1];
  //   product_row_2 = product_row[2]; product_row_3 = product_row[3]; product_row_4 = product_row[4];
  //   product_row_5 = product_row[5]; product_row_6 = product_row[6]; product_row_7 = product_row[7]
endmodule

module bitwise_or_8_8 (
  input  [7:0] x_row_0,
  input  [7:0] x_row_1,
  input  [7:0] x_row_2,
  input  [7:0] x_row_3,
  input  [7:0] x_row_4,
  input  [7:0] x_row_5,
  input  [7:0] x_row_6,
  input  [7:0] x_row_7,
  input  [7:0] y_row_0,
  input  [7:0] y_row_1,
  input  [7:0] y_row_2,
  input  [7:0] y_row_3,
  input  [7:0] y_row_4,
  input  [7:0] y_row_5,
  input  [7:0] y_row_6,
  input  [7:0] y_row_7,
  output [7:0] z_row_0,
  output [7:0] z_row_1,
  output [7:0] z_row_2,
  output [7:0] z_row_3,
  output [7:0] z_row_4,
  output [7:0] z_row_5,
  output [7:0] z_row_6,
  output [7:0] z_row_7
);

  or or_1 (z_row_1[0], x_row_1[0], y_row_1[0]);
  or or_2 (z_row_1[1], x_row_1[1], y_row_1[1]);
  or or_3 (z_row_1[2], x_row_1[2], y_row_1[2]);
  or or_4 (z_row_1[3], x_row_1[3], y_row_1[3]);
  or or_5 (z_row_1[4], x_row_1[4], y_row_1[4]);
  or or_6 (z_row_1[5], x_row_1[5], y_row_1[5]);
  or or_7 (z_row_1[6], x_row_1[6], y_row_1[6]);
  or or_8 (z_row_1[7], x_row_1[7], y_row_1[7]);
  or or_9 (z_row_2[0], x_row_2[0], y_row_2[0]);
  or or_10 (z_row_2[1], x_row_2[1], y_row_2[1]);
  or or_11 (z_row_2[2], x_row_2[2], y_row_2[2]);
  or or_12 (z_row_2[3], x_row_2[3], y_row_2[3]);
  or or_13 (z_row_2[4], x_row_2[4], y_row_2[4]);
  or or_14 (z_row_2[5], x_row_2[5], y_row_2[5]);
  or or_15 (z_row_2[6], x_row_2[6], y_row_2[6]);
  or or_16 (z_row_2[7], x_row_2[7], y_row_2[7]);
  or or_17 (z_row_3[0], x_row_3[0], y_row_3[0]);
  or or_18 (z_row_3[1], x_row_3[1], y_row_3[1]);
  or or_19 (z_row_3[2], x_row_3[2], y_row_3[2]);
  or or_20 (z_row_3[3], x_row_3[3], y_row_3[3]);
  or or_21 (z_row_3[4], x_row_3[4], y_row_3[4]);
  or or_22 (z_row_3[5], x_row_3[5], y_row_3[5]);
  or or_23 (z_row_3[6], x_row_3[6], y_row_3[6]);
  or or_24 (z_row_3[7], x_row_3[7], y_row_3[7]);
  or or_25 (z_row_4[0], x_row_4[0], y_row_4[0]);
  or or_26 (z_row_4[1], x_row_4[1], y_row_4[1]);
  or or_27 (z_row_4[2], x_row_4[2], y_row_4[2]);
  or or_28 (z_row_4[3], x_row_4[3], y_row_4[3]);
  or or_29 (z_row_4[4], x_row_4[4], y_row_4[4]);
  or or_30 (z_row_4[5], x_row_4[5], y_row_4[5]);
  or or_31 (z_row_4[6], x_row_4[6], y_row_4[6]);
  or or_32 (z_row_4[7], x_row_4[7], y_row_4[7]);
  DotMatrix #(.inputtype("row"), .matrixcols(8), .matrixrows(8)) dotmatrix_1 (
    .row0(x_row_0), .row1(x_row_1), .row2(x_row_2), .row3(x_row_3), .row4(x_row_4), .row5(x_row_5),
    .row6(x_row_6), .row7(x_row_7));
  DotMatrix #(.inputtype("row"), .matrixcols(8), .matrixrows(8)) dotmatrix_2 (
    .row0(y_row_0), .row1(y_row_1), .row2(y_row_2), .row3(y_row_3), .row4(y_row_4), .row5(y_row_5),
    .row6(y_row_6), .row7(y_row_7));
  or or_33 (z_row_0[0], x_row_0[0], y_row_0[0]);
  or or_34 (z_row_0[1], x_row_0[1], y_row_0[1]);
  or or_35 (z_row_0[2], x_row_0[2], y_row_0[2]);
  or or_36 (z_row_0[3], x_row_0[3], y_row_0[3]);
  or or_37 (z_row_0[4], x_row_0[4], y_row_0[4]);
  or or_38 (z_row_0[5], x_row_0[5], y_row_0[5]);
  or or_39 (z_row_0[6], x_row_0[6], y_row_0[6]);
  or or_40 (z_row_0[7], x_row_0[7], y_row_0[7]);
  DotMatrix #(.inputtype("row"), .matrixcols(8), .matrixrows(8)) dotmatrix_3 (
    .row0(z_row_0), .row1(z_row_1), .row2(z_row_2), .row3(z_row_3), .row4(z_row_4), .row5(z_row_5),
    .row6(z_row_6), .row7(z_row_7));
  or or_41 (z_row_5[0], x_row_5[0], y_row_5[0]);
  or or_42 (z_row_5[1], x_row_5[1], y_row_5[1]);
  or or_43 (z_row_5[2], x_row_5[2], y_row_5[2]);
  or or_44 (z_row_5[3], x_row_5[3], y_row_5[3]);
  or or_45 (z_row_5[4], x_row_5[4], y_row_5[4]);
  or or_46 (z_row_5[5], x_row_5[5], y_row_5[5]);
  or or_47 (z_row_5[6], x_row_5[6], y_row_5[6]);
  or or_48 (z_row_5[7], x_row_5[7], y_row_5[7]);
  or or_49 (z_row_6[0], x_row_6[0], y_row_6[0]);
  or or_50 (z_row_6[1], x_row_6[1], y_row_6[1]);
  or or_51 (z_row_6[2], x_row_6[2], y_row_6[2]);
  or or_52 (z_row_6[3], x_row_6[3], y_row_6[3]);
  or or_53 (z_row_6[4], x_row_6[4], y_row_6[4]);
  or or_54 (z_row_6[5], x_row_6[5], y_row_6[5]);
  or or_55 (z_row_6[6], x_row_6[6], y_row_6[6]);
  or or_56 (z_row_6[7], x_row_6[7], y_row_6[7]);
  or or_57 (z_row_7[0], x_row_7[0], y_row_7[0]);
  or or_58 (z_row_7[1], x_row_7[1], y_row_7[1]);
  or or_59 (z_row_7[2], x_row_7[2], y_row_7[2]);
  or or_60 (z_row_7[3], x_row_7[3], y_row_7[3]);
  or or_61 (z_row_7[4], x_row_7[4], y_row_7[4]);
  or or_62 (z_row_7[5], x_row_7[5], y_row_7[5]);
  or or_63 (z_row_7[6], x_row_7[6], y_row_7[6]);
  or or_64 (z_row_7[7], x_row_7[7], y_row_7[7]);

  // Other names for the same wires on the sheet: x00 = x_row_0[0]; x01 = x_row_0[1]; x02 = x_row_0[2];
  //   x03 = x_row_0[3]; x04 = x_row_0[4]; x05 = x_row_0[5]; x06 = x_row_0[6]; x07 = x_row_0[7]; x10 = x_row_1[0];
  //   x11 = x_row_1[1]; x12 = x_row_1[2]; x13 = x_row_1[3]; x14 = x_row_1[4]; x15 = x_row_1[5]; x16 = x_row_1[6];
  //   x17 = x_row_1[7]; x20 = x_row_2[0]; x21 = x_row_2[1]; x22 = x_row_2[2]; x23 = x_row_2[3]; x24 = x_row_2[4];
  //   x25 = x_row_2[5]; x26 = x_row_2[6]; x27 = x_row_2[7]; x30 = x_row_3[0]; x31 = x_row_3[1]; x32 = x_row_3[2];
  //   x33 = x_row_3[3]; x34 = x_row_3[4]; x35 = x_row_3[5]; x36 = x_row_3[6]; x37 = x_row_3[7]; x40 = x_row_4[0];
  //   x41 = x_row_4[1]; x42 = x_row_4[2]; x43 = x_row_4[3]; x44 = x_row_4[4]; x45 = x_row_4[5]; x46 = x_row_4[6];
  //   x47 = x_row_4[7]; x50 = x_row_5[0]; x51 = x_row_5[1]; x52 = x_row_5[2]; x53 = x_row_5[3]; x54 = x_row_5[4];
  //   x55 = x_row_5[5]; x56 = x_row_5[6]; x57 = x_row_5[7]; x60 = x_row_6[0]; x61 = x_row_6[1]; x62 = x_row_6[2];
  //   x63 = x_row_6[3]; x64 = x_row_6[4]; x65 = x_row_6[5]; x66 = x_row_6[6]; x67 = x_row_6[7]; x70 = x_row_7[0];
  //   x71 = x_row_7[1]; x72 = x_row_7[2]; x73 = x_row_7[3]; x74 = x_row_7[4]; x75 = x_row_7[5]; x76 = x_row_7[6];
  //   x77 = x_row_7[7]; y00 = y_row_0[0]; y01 = y_row_0[1]; y02 = y_row_0[2]; y03 = y_row_0[3]; y04 = y_row_0[4];
  //   y05 = y_row_0[5]; y06 = y_row_0[6]; y07 = y_row_0[7]; y10 = y_row_1[0]; y11 = y_row_1[1]; y12 = y_row_1[2];
  //   y13 = y_row_1[3]; y14 = y_row_1[4]; y15 = y_row_1[5]; y16 = y_row_1[6]; y17 = y_row_1[7]; y20 = y_row_2[0];
  //   y21 = y_row_2[1]; y22 = y_row_2[2]; y23 = y_row_2[3]; y24 = y_row_2[4]; y25 = y_row_2[5]; y26 = y_row_2[6];
  //   y27 = y_row_2[7]; y30 = y_row_3[0]; y31 = y_row_3[1]; y32 = y_row_3[2]; y33 = y_row_3[3]; y34 = y_row_3[4];
  //   y35 = y_row_3[5]; y36 = y_row_3[6]; y37 = y_row_3[7]; y40 = y_row_4[0]; y41 = y_row_4[1]; y42 = y_row_4[2];
  //   y43 = y_row_4[3]; y44 = y_row_4[4]; y45 = y_row_4[5]; y46 = y_row_4[6]; y47 = y_row_4[7]; y50 = y_row_5[0];
  //   y51 = y_row_5[1]; y52 = y_row_5[2]; y53 = y_row_5[3]; y54 = y_row_5[4]; y55 = y_row_5[5]; y56 = y_row_5[6];
  //   y57 = y_row_5[7]; y60 = y_row_6[0]; y61 = y_row_6[1]; y62 = y_row_6[2]; y63 = y_row_6[3]; y64 = y_row_6[4];
  //   y65 = y_row_6[5]; y66 = y_row_6[6]; y67 = y_row_6[7]; y70 = y_row_7[0]; y71 = y_row_7[1]; y72 = y_row_7[2];
  //   y73 = y_row_7[3]; y74 = y_row_7[4]; y75 = y_row_7[5]; y76 = y_row_7[6]; y77 = y_row_7[7]
endmodule

module is_connected (
  input  [7:0] x_row_0,
  input  [7:0] x_row_1,
  input  [7:0] x_row_2,
  input  [7:0] x_row_3,
  input  [7:0] x_row_4,
  input  [7:0] x_row_5,
  input  [7:0] x_row_6,
  input  [7:0] x_row_7,
  output is_connected
);

  wire [7:0] ans_mat_0, ans_mat_1, ans_mat_2, ans_mat_3, ans_mat_4, ans_mat_5, ans_mat_6, ans_mat_7,
       bitwise_or_8_8_1_z_row_0, bitwise_or_8_8_1_z_row_1, bitwise_or_8_8_1_z_row_2,
       bitwise_or_8_8_1_z_row_3, bitwise_or_8_8_1_z_row_4, bitwise_or_8_8_1_z_row_5,
       bitwise_or_8_8_1_z_row_6, bitwise_or_8_8_1_z_row_7, bitwise_or_8_8_2_z_row_0,
       bitwise_or_8_8_2_z_row_1, bitwise_or_8_8_2_z_row_2, bitwise_or_8_8_2_z_row_3,
       bitwise_or_8_8_2_z_row_4, bitwise_or_8_8_2_z_row_5, bitwise_or_8_8_2_z_row_6,
       bitwise_or_8_8_2_z_row_7, bitwise_or_8_8_3_z_row_0, bitwise_or_8_8_3_z_row_1,
       bitwise_or_8_8_3_z_row_2, bitwise_or_8_8_3_z_row_3, bitwise_or_8_8_3_z_row_4,
       bitwise_or_8_8_3_z_row_5, bitwise_or_8_8_3_z_row_6, bitwise_or_8_8_3_z_row_7,
       bitwise_or_8_8_4_z_row_0, bitwise_or_8_8_4_z_row_1, bitwise_or_8_8_4_z_row_2,
       bitwise_or_8_8_4_z_row_3, bitwise_or_8_8_4_z_row_4, bitwise_or_8_8_4_z_row_5,
       bitwise_or_8_8_4_z_row_6, bitwise_or_8_8_4_z_row_7, bitwise_or_8_8_5_z_row_0,
       bitwise_or_8_8_5_z_row_1, bitwise_or_8_8_5_z_row_2, bitwise_or_8_8_5_z_row_3,
       bitwise_or_8_8_5_z_row_4, bitwise_or_8_8_5_z_row_5, bitwise_or_8_8_5_z_row_6,
       bitwise_or_8_8_5_z_row_7, bitwise_or_8_8_6_z_row_0, bitwise_or_8_8_6_z_row_1,
       bitwise_or_8_8_6_z_row_2, bitwise_or_8_8_6_z_row_3, bitwise_or_8_8_6_z_row_4,
       bitwise_or_8_8_6_z_row_5, bitwise_or_8_8_6_z_row_6, bitwise_or_8_8_6_z_row_7, mat12_0, mat12_1,
       mat12_2, mat12_3, mat12_4, mat12_5, mat12_6, mat12_7, mat123_0, mat123_1, mat123_2, mat123_3,
       mat123_4, mat123_5, mat123_6, mat123_7, mat1234_0, mat1234_1, mat1234_2, mat1234_3, mat1234_4,
       mat1234_5, mat1234_6, mat1234_7, mat12345_0, mat12345_1, mat12345_2, mat12345_3, mat12345_4,
       mat12345_5, mat12345_6, mat12345_7, mat123456_0, mat123456_1, mat123456_2, mat123456_3, mat123456_4,
       mat123456_5, mat123456_6, mat123456_7, mat1234567_0, mat1234567_1, mat1234567_2, mat1234567_3,
       mat1234567_4, mat1234567_5, mat1234567_6, mat1234567_7;

  matmul matmul_1 (
    .x_row_0(mat123456_0), .x_row_1(mat123456_1), .x_row_2(mat123456_2), .x_row_3(mat123456_3),
    .x_row_4(mat123456_4), .x_row_5(mat123456_5), .x_row_6(mat123456_6), .x_row_7(mat123456_7),
    .y_row_0(x_row_0), .y_row_1(x_row_1), .y_row_2(x_row_2), .y_row_3(x_row_3), .y_row_4(x_row_4),
    .y_row_5(x_row_5), .y_row_6(x_row_6), .y_row_7(x_row_7), .z_row_0(mat1234567_0), .z_row_1(mat1234567_1),
    .z_row_2(mat1234567_2), .z_row_3(mat1234567_3), .z_row_4(mat1234567_4), .z_row_5(mat1234567_5),
    .z_row_6(mat1234567_6), .z_row_7(mat1234567_7));
  matmul matmul_2 (
    .x_row_0(x_row_0), .x_row_1(x_row_1), .x_row_2(x_row_2), .x_row_3(x_row_3), .x_row_4(x_row_4),
    .x_row_5(x_row_5), .x_row_6(x_row_6), .x_row_7(x_row_7), .y_row_0(x_row_0), .y_row_1(x_row_1),
    .y_row_2(x_row_2), .y_row_3(x_row_3), .y_row_4(x_row_4), .y_row_5(x_row_5), .y_row_6(x_row_6),
    .y_row_7(x_row_7), .z_row_0(mat12_0), .z_row_1(mat12_1), .z_row_2(mat12_2), .z_row_3(mat12_3),
    .z_row_4(mat12_4), .z_row_5(mat12_5), .z_row_6(mat12_6), .z_row_7(mat12_7));
  matmul matmul_3 (
    .x_row_0(mat12_0), .x_row_1(mat12_1), .x_row_2(mat12_2), .x_row_3(mat12_3), .x_row_4(mat12_4),
    .x_row_5(mat12_5), .x_row_6(mat12_6), .x_row_7(mat12_7), .y_row_0(x_row_0), .y_row_1(x_row_1),
    .y_row_2(x_row_2), .y_row_3(x_row_3), .y_row_4(x_row_4), .y_row_5(x_row_5), .y_row_6(x_row_6),
    .y_row_7(x_row_7), .z_row_0(mat123_0), .z_row_1(mat123_1), .z_row_2(mat123_2), .z_row_3(mat123_3),
    .z_row_4(mat123_4), .z_row_5(mat123_5), .z_row_6(mat123_6), .z_row_7(mat123_7));
  matmul matmul_4 (
    .x_row_0(mat123_0), .x_row_1(mat123_1), .x_row_2(mat123_2), .x_row_3(mat123_3), .x_row_4(mat123_4),
    .x_row_5(mat123_5), .x_row_6(mat123_6), .x_row_7(mat123_7), .y_row_0(x_row_0), .y_row_1(x_row_1),
    .y_row_2(x_row_2), .y_row_3(x_row_3), .y_row_4(x_row_4), .y_row_5(x_row_5), .y_row_6(x_row_6),
    .y_row_7(x_row_7), .z_row_0(mat1234_0), .z_row_1(mat1234_1), .z_row_2(mat1234_2), .z_row_3(mat1234_3),
    .z_row_4(mat1234_4), .z_row_5(mat1234_5), .z_row_6(mat1234_6), .z_row_7(mat1234_7));
  matmul matmul_5 (
    .x_row_0(mat1234_0), .x_row_1(mat1234_1), .x_row_2(mat1234_2), .x_row_3(mat1234_3), .x_row_4(mat1234_4),
    .x_row_5(mat1234_5), .x_row_6(mat1234_6), .x_row_7(mat1234_7), .y_row_0(x_row_0), .y_row_1(x_row_1),
    .y_row_2(x_row_2), .y_row_3(x_row_3), .y_row_4(x_row_4), .y_row_5(x_row_5), .y_row_6(x_row_6),
    .y_row_7(x_row_7), .z_row_0(mat12345_0), .z_row_1(mat12345_1), .z_row_2(mat12345_2),
    .z_row_3(mat12345_3), .z_row_4(mat12345_4), .z_row_5(mat12345_5), .z_row_6(mat12345_6),
    .z_row_7(mat12345_7));
  matmul matmul_6 (
    .x_row_0(mat12345_0), .x_row_1(mat12345_1), .x_row_2(mat12345_2), .x_row_3(mat12345_3),
    .x_row_4(mat12345_4), .x_row_5(mat12345_5), .x_row_6(mat12345_6), .x_row_7(mat12345_7),
    .y_row_0(x_row_0), .y_row_1(x_row_1), .y_row_2(x_row_2), .y_row_3(x_row_3), .y_row_4(x_row_4),
    .y_row_5(x_row_5), .y_row_6(x_row_6), .y_row_7(x_row_7), .z_row_0(mat123456_0), .z_row_1(mat123456_1),
    .z_row_2(mat123456_2), .z_row_3(mat123456_3), .z_row_4(mat123456_4), .z_row_5(mat123456_5),
    .z_row_6(mat123456_6), .z_row_7(mat123456_7));
  DotMatrix #(.inputtype("row"), .matrixcols(8), .matrixrows(8)) dotmatrix_1 (
    .row0(x_row_0), .row1(x_row_1), .row2(x_row_2), .row3(x_row_3), .row4(x_row_4), .row5(x_row_5),
    .row6(x_row_6), .row7(x_row_7));
  bitwise_or_8_8 bitwise_or_8_8_1 (
    .x_row_0(x_row_0), .x_row_1(x_row_1), .x_row_2(x_row_2), .x_row_3(x_row_3), .x_row_4(x_row_4),
    .x_row_5(x_row_5), .x_row_6(x_row_6), .x_row_7(x_row_7), .y_row_0(mat12_0), .y_row_1(mat12_1),
    .y_row_2(mat12_2), .y_row_3(mat12_3), .y_row_4(mat12_4), .y_row_5(mat12_5), .y_row_6(mat12_6),
    .y_row_7(mat12_7), .z_row_0(bitwise_or_8_8_1_z_row_0), .z_row_1(bitwise_or_8_8_1_z_row_1),
    .z_row_2(bitwise_or_8_8_1_z_row_2), .z_row_3(bitwise_or_8_8_1_z_row_3),
    .z_row_4(bitwise_or_8_8_1_z_row_4), .z_row_5(bitwise_or_8_8_1_z_row_5),
    .z_row_6(bitwise_or_8_8_1_z_row_6), .z_row_7(bitwise_or_8_8_1_z_row_7));
  bitwise_or_8_8 bitwise_or_8_8_2 (
    .x_row_0(mat123_0), .x_row_1(mat123_1), .x_row_2(mat123_2), .x_row_3(mat123_3), .x_row_4(mat123_4),
    .x_row_5(mat123_5), .x_row_6(mat123_6), .x_row_7(mat123_7), .y_row_0(mat1234_0), .y_row_1(mat1234_1),
    .y_row_2(mat1234_2), .y_row_3(mat1234_3), .y_row_4(mat1234_4), .y_row_5(mat1234_5), .y_row_6(mat1234_6),
    .y_row_7(mat1234_7), .z_row_0(bitwise_or_8_8_2_z_row_0), .z_row_1(bitwise_or_8_8_2_z_row_1),
    .z_row_2(bitwise_or_8_8_2_z_row_2), .z_row_3(bitwise_or_8_8_2_z_row_3),
    .z_row_4(bitwise_or_8_8_2_z_row_4), .z_row_5(bitwise_or_8_8_2_z_row_5),
    .z_row_6(bitwise_or_8_8_2_z_row_6), .z_row_7(bitwise_or_8_8_2_z_row_7));
  bitwise_or_8_8 bitwise_or_8_8_3 (
    .x_row_0(mat12345_0), .x_row_1(mat12345_1), .x_row_2(mat12345_2), .x_row_3(mat12345_3),
    .x_row_4(mat12345_4), .x_row_5(mat12345_5), .x_row_6(mat12345_6), .x_row_7(mat12345_7),
    .y_row_0(mat123456_0), .y_row_1(mat123456_1), .y_row_2(mat123456_2), .y_row_3(mat123456_3),
    .y_row_4(mat123456_4), .y_row_5(mat123456_5), .y_row_6(mat123456_6), .y_row_7(mat123456_7),
    .z_row_0(bitwise_or_8_8_3_z_row_0), .z_row_1(bitwise_or_8_8_3_z_row_1),
    .z_row_2(bitwise_or_8_8_3_z_row_2), .z_row_3(bitwise_or_8_8_3_z_row_3),
    .z_row_4(bitwise_or_8_8_3_z_row_4), .z_row_5(bitwise_or_8_8_3_z_row_5),
    .z_row_6(bitwise_or_8_8_3_z_row_6), .z_row_7(bitwise_or_8_8_3_z_row_7));
  bitwise_or_8_8 bitwise_or_8_8_4 (
    .x_row_0(mat1234567_0), .x_row_1(mat1234567_1), .x_row_2(mat1234567_2), .x_row_3(mat1234567_3),
    .x_row_4(mat1234567_4), .x_row_5(mat1234567_5), .x_row_6(mat1234567_6), .x_row_7(mat1234567_7),
    .y_row_0(8'h80), .y_row_1(8'h40), .y_row_2(8'h20), .y_row_3(8'h10), .y_row_4(8'h8), .y_row_5(8'h4),
    .y_row_6(8'h2), .y_row_7(8'h1), .z_row_0(bitwise_or_8_8_4_z_row_0), .z_row_1(bitwise_or_8_8_4_z_row_1),
    .z_row_2(bitwise_or_8_8_4_z_row_2), .z_row_3(bitwise_or_8_8_4_z_row_3),
    .z_row_4(bitwise_or_8_8_4_z_row_4), .z_row_5(bitwise_or_8_8_4_z_row_5),
    .z_row_6(bitwise_or_8_8_4_z_row_6), .z_row_7(bitwise_or_8_8_4_z_row_7));
  matrix_and_8_8 matrix_and_8_8_1 (
    .x_row_0(ans_mat_0), .x_row_1(ans_mat_1), .x_row_2(ans_mat_2), .x_row_3(ans_mat_3), .x_row_4(ans_mat_4),
    .x_row_5(ans_mat_5), .x_row_6(ans_mat_6), .x_row_7(ans_mat_7), .z(is_connected));
  bitwise_or_8_8 bitwise_or_8_8_5 (
    .x_row_0(bitwise_or_8_8_1_z_row_0), .x_row_1(bitwise_or_8_8_1_z_row_1),
    .x_row_2(bitwise_or_8_8_1_z_row_2), .x_row_3(bitwise_or_8_8_1_z_row_3),
    .x_row_4(bitwise_or_8_8_1_z_row_4), .x_row_5(bitwise_or_8_8_1_z_row_5),
    .x_row_6(bitwise_or_8_8_1_z_row_6), .x_row_7(bitwise_or_8_8_1_z_row_7),
    .y_row_0(bitwise_or_8_8_2_z_row_0), .y_row_1(bitwise_or_8_8_2_z_row_1),
    .y_row_2(bitwise_or_8_8_2_z_row_2), .y_row_3(bitwise_or_8_8_2_z_row_3),
    .y_row_4(bitwise_or_8_8_2_z_row_4), .y_row_5(bitwise_or_8_8_2_z_row_5),
    .y_row_6(bitwise_or_8_8_2_z_row_6), .y_row_7(bitwise_or_8_8_2_z_row_7),
    .z_row_0(bitwise_or_8_8_5_z_row_0), .z_row_1(bitwise_or_8_8_5_z_row_1),
    .z_row_2(bitwise_or_8_8_5_z_row_2), .z_row_3(bitwise_or_8_8_5_z_row_3),
    .z_row_4(bitwise_or_8_8_5_z_row_4), .z_row_5(bitwise_or_8_8_5_z_row_5),
    .z_row_6(bitwise_or_8_8_5_z_row_6), .z_row_7(bitwise_or_8_8_5_z_row_7));
  bitwise_or_8_8 bitwise_or_8_8_6 (
    .x_row_0(bitwise_or_8_8_3_z_row_0), .x_row_1(bitwise_or_8_8_3_z_row_1),
    .x_row_2(bitwise_or_8_8_3_z_row_2), .x_row_3(bitwise_or_8_8_3_z_row_3),
    .x_row_4(bitwise_or_8_8_3_z_row_4), .x_row_5(bitwise_or_8_8_3_z_row_5),
    .x_row_6(bitwise_or_8_8_3_z_row_6), .x_row_7(bitwise_or_8_8_3_z_row_7),
    .y_row_0(bitwise_or_8_8_4_z_row_0), .y_row_1(bitwise_or_8_8_4_z_row_1),
    .y_row_2(bitwise_or_8_8_4_z_row_2), .y_row_3(bitwise_or_8_8_4_z_row_3),
    .y_row_4(bitwise_or_8_8_4_z_row_4), .y_row_5(bitwise_or_8_8_4_z_row_5),
    .y_row_6(bitwise_or_8_8_4_z_row_6), .y_row_7(bitwise_or_8_8_4_z_row_7),
    .z_row_0(bitwise_or_8_8_6_z_row_0), .z_row_1(bitwise_or_8_8_6_z_row_1),
    .z_row_2(bitwise_or_8_8_6_z_row_2), .z_row_3(bitwise_or_8_8_6_z_row_3),
    .z_row_4(bitwise_or_8_8_6_z_row_4), .z_row_5(bitwise_or_8_8_6_z_row_5),
    .z_row_6(bitwise_or_8_8_6_z_row_6), .z_row_7(bitwise_or_8_8_6_z_row_7));
  bitwise_or_8_8 bitwise_or_8_8_7 (
    .x_row_0(bitwise_or_8_8_5_z_row_0), .x_row_1(bitwise_or_8_8_5_z_row_1),
    .x_row_2(bitwise_or_8_8_5_z_row_2), .x_row_3(bitwise_or_8_8_5_z_row_3),
    .x_row_4(bitwise_or_8_8_5_z_row_4), .x_row_5(bitwise_or_8_8_5_z_row_5),
    .x_row_6(bitwise_or_8_8_5_z_row_6), .x_row_7(bitwise_or_8_8_5_z_row_7),
    .y_row_0(bitwise_or_8_8_6_z_row_0), .y_row_1(bitwise_or_8_8_6_z_row_1),
    .y_row_2(bitwise_or_8_8_6_z_row_2), .y_row_3(bitwise_or_8_8_6_z_row_3),
    .y_row_4(bitwise_or_8_8_6_z_row_4), .y_row_5(bitwise_or_8_8_6_z_row_5),
    .y_row_6(bitwise_or_8_8_6_z_row_6), .y_row_7(bitwise_or_8_8_6_z_row_7), .z_row_0(ans_mat_0),
    .z_row_1(ans_mat_1), .z_row_2(ans_mat_2), .z_row_3(ans_mat_3), .z_row_4(ans_mat_4), .z_row_5(ans_mat_5),
    .z_row_6(ans_mat_6), .z_row_7(ans_mat_7));
endmodule

module matrix_and_8_8 (
  input  [7:0] x_row_0,
  input  [7:0] x_row_1,
  input  [7:0] x_row_2,
  input  [7:0] x_row_3,
  input  [7:0] x_row_4,
  input  [7:0] x_row_5,
  input  [7:0] x_row_6,
  input  [7:0] x_row_7,
  output z
);

  wire and_1_out, and_2_out, and_3_out, and_4_out, and_5_out, and_6_out, and_7_out, and_8_out, and_9_out,
       and_10_out, and_11_out, and_12_out, and_13_out, and_14_out, and_15_out, and_16_out, and_17_out,
       and_18_out, and_19_out, and_20_out, and_21_out, and_22_out, and_23_out, and_24_out, and_25_out,
       and_26_out, and_27_out, and_28_out, and_29_out, and_30_out, and_31_out, and_33_out, and_34_out,
       and_35_out, and_36_out, and_37_out, and_38_out, and_39_out, and_40_out, and_41_out, and_42_out,
       and_43_out, and_44_out, and_45_out, and_46_out, and_47_out, and_48_out, and_49_out, and_50_out,
       and_51_out, and_52_out, and_53_out, and_54_out, and_55_out, and_56_out, and_57_out, and_58_out,
       and_59_out, and_60_out, and_61_out, and_62_out, and_63_out;

  DotMatrix #(.inputtype("row"), .matrixcols(8), .matrixrows(8)) dotmatrix_1 (
    .row0(x_row_0), .row1(x_row_1), .row2(x_row_2), .row3(x_row_3), .row4(x_row_4), .row5(x_row_5),
    .row6(x_row_6), .row7(x_row_7));
  and and_1 (and_1_out, x_row_0[0], x_row_0[1]);
  and and_2 (and_2_out, x_row_0[2], x_row_0[3]);
  and and_3 (and_3_out, x_row_0[4], x_row_0[5]);
  and and_4 (and_4_out, x_row_0[6], x_row_0[7]);
  and and_5 (and_5_out, x_row_1[0], x_row_1[1]);
  and and_6 (and_6_out, x_row_1[2], x_row_1[3]);
  and and_7 (and_7_out, x_row_1[4], x_row_1[5]);
  and and_8 (and_8_out, x_row_1[6], x_row_1[7]);
  and and_9 (and_9_out, x_row_2[0], x_row_2[1]);
  and and_10 (and_10_out, x_row_2[2], x_row_2[3]);
  and and_11 (and_11_out, x_row_2[4], x_row_2[5]);
  and and_12 (and_12_out, x_row_2[6], x_row_2[7]);
  and and_13 (and_13_out, x_row_3[0], x_row_3[1]);
  and and_14 (and_14_out, x_row_3[2], x_row_3[3]);
  and and_15 (and_15_out, x_row_3[4], x_row_3[5]);
  and and_16 (and_16_out, x_row_3[6], x_row_3[7]);
  and and_17 (and_17_out, and_1_out, and_2_out);
  and and_18 (and_18_out, and_17_out, and_19_out);
  and and_19 (and_19_out, and_3_out, and_4_out);
  and and_20 (and_20_out, and_5_out, and_6_out);
  and and_21 (and_21_out, and_20_out, and_22_out);
  and and_22 (and_22_out, and_7_out, and_8_out);
  and and_23 (and_23_out, and_9_out, and_10_out);
  and and_24 (and_24_out, and_23_out, and_25_out);
  and and_25 (and_25_out, and_11_out, and_12_out);
  and and_26 (and_26_out, and_13_out, and_14_out);
  and and_27 (and_27_out, and_26_out, and_28_out);
  and and_28 (and_28_out, and_15_out, and_16_out);
  and and_29 (and_29_out, and_18_out, and_21_out);
  and and_30 (and_30_out, and_24_out, and_27_out);
  and and_31 (and_31_out, and_29_out, and_30_out);
  and and_32 (z, and_31_out, and_63_out);
  and and_33 (and_33_out, x_row_4[0], x_row_4[1]);
  and and_34 (and_34_out, x_row_4[2], x_row_4[3]);
  and and_35 (and_35_out, x_row_4[4], x_row_4[5]);
  and and_36 (and_36_out, x_row_4[6], x_row_4[7]);
  and and_37 (and_37_out, x_row_5[0], x_row_5[1]);
  and and_38 (and_38_out, x_row_5[2], x_row_5[3]);
  and and_39 (and_39_out, x_row_5[4], x_row_5[5]);
  and and_40 (and_40_out, x_row_5[6], x_row_5[7]);
  and and_41 (and_41_out, x_row_6[0], x_row_6[1]);
  and and_42 (and_42_out, x_row_6[2], x_row_6[3]);
  and and_43 (and_43_out, x_row_6[4], x_row_6[5]);
  and and_44 (and_44_out, x_row_6[6], x_row_6[7]);
  and and_45 (and_45_out, x_row_7[0], x_row_7[1]);
  and and_46 (and_46_out, x_row_7[2], x_row_7[3]);
  and and_47 (and_47_out, x_row_7[4], x_row_7[5]);
  and and_48 (and_48_out, x_row_7[6], x_row_7[7]);
  and and_49 (and_49_out, and_33_out, and_34_out);
  and and_50 (and_50_out, and_49_out, and_51_out);
  and and_51 (and_51_out, and_35_out, and_36_out);
  and and_52 (and_52_out, and_37_out, and_38_out);
  and and_53 (and_53_out, and_52_out, and_54_out);
  and and_54 (and_54_out, and_39_out, and_40_out);
  and and_55 (and_55_out, and_41_out, and_42_out);
  and and_56 (and_56_out, and_55_out, and_57_out);
  and and_57 (and_57_out, and_43_out, and_44_out);
  and and_58 (and_58_out, and_45_out, and_46_out);
  and and_59 (and_59_out, and_58_out, and_60_out);
  and and_60 (and_60_out, and_47_out, and_48_out);
  and and_61 (and_61_out, and_50_out, and_53_out);
  and and_62 (and_62_out, and_56_out, and_59_out);
  and and_63 (and_63_out, and_61_out, and_62_out);
endmodule

module is_fully_connected (
  input  [7:0] x_row_0,
  input  [7:0] x_row_1,
  input  [7:0] x_row_2,
  input  [7:0] x_row_3,
  input  [7:0] x_row_4,
  input  [7:0] x_row_5,
  input  [7:0] x_row_6,
  input  [7:0] x_row_7,
  output is_fully_connected
);

  wire [7:0] ans_mat_0, ans_mat_1, ans_mat_2, ans_mat_3, ans_mat_4, ans_mat_5, ans_mat_6, ans_mat_7;

  bitwise_or_8_8 bitwise_or_8_8_1 (
    .x_row_0(x_row_0), .x_row_1(x_row_1), .x_row_2(x_row_2), .x_row_3(x_row_3), .x_row_4(x_row_4),
    .x_row_5(x_row_5), .x_row_6(x_row_6), .x_row_7(x_row_7), .y_row_0(8'h80), .y_row_1(8'h40),
    .y_row_2(8'h20), .y_row_3(8'h10), .y_row_4(8'h8), .y_row_5(8'h4), .y_row_6(8'h2), .y_row_7(8'h1),
    .z_row_0(ans_mat_0), .z_row_1(ans_mat_1), .z_row_2(ans_mat_2), .z_row_3(ans_mat_3), .z_row_4(ans_mat_4),
    .z_row_5(ans_mat_5), .z_row_6(ans_mat_6), .z_row_7(ans_mat_7));
  DotMatrix #(.inputtype("row"), .matrixcols(8), .matrixrows(8)) dotmatrix_1 (
    .row0(x_row_0), .row1(x_row_1), .row2(x_row_2), .row3(x_row_3), .row4(x_row_4), .row5(x_row_5),
    .row6(x_row_6), .row7(x_row_7));
  matrix_and_8_8 matrix_and_8_8_1 (
    .x_row_0(ans_mat_0), .x_row_1(ans_mat_1), .x_row_2(ans_mat_2), .x_row_3(ans_mat_3), .x_row_4(ans_mat_4),
    .x_row_5(ans_mat_5), .x_row_6(ans_mat_6), .x_row_7(ans_mat_7), .z(is_fully_connected));
endmodule

module exactly (
  input  [7:0] x_row_0,
  input  [7:0] x_row_1,
  input  [7:0] x_row_2,
  input  [7:0] x_row_3,
  input  [7:0] x_row_4,
  input  [7:0] x_row_5,
  input  [7:0] x_row_6,
  input  [7:0] x_row_7,
  input  [2:0] from,
  input  [2:0] to,
  input  [2:0] num_steps,
  output path_exists
);

  wire and_1_out, and_3_out, ans1, ans12, ans123, ans1234, ans12345, ans123456, ans1234567, loop, row400,
       row411, row422, row433, row444, row455, row466, row477, row500, row511, row522, row533, row544,
       row555, row566, row577, row600, row611, row622, row633, row644, row655, row666, row677, row700,
       row711, row722, row733, row744, row755, row766, row777, xnor_1_out, xnor_2_out, xnor_3_out;
  wire [7:0] mat12_0, mat12_1, mat12_2, mat12_3, mat12_4, mat12_5, mat12_6, mat12_7, mat123_0, mat123_1,
       mat123_2, mat123_3, mat123_4, mat123_5, mat123_6, mat123_7, mat1234_0, mat1234_1, mat1234_2,
       mat1234_3, mat1234_4, mat1234_5, mat1234_6, mat1234_7, mat12345_0, mat12345_1, mat12345_2, mat12345_3,
       mat12345_4, mat12345_5, mat12345_6, mat12345_7, mat123456_0, mat123456_1, mat123456_2, mat123456_3,
       mat123456_4, mat123456_5, mat123456_6, mat123456_7, mat1234567_0, mat1234567_1, mat1234567_2,
       mat1234567_3, mat1234567_4, mat1234567_5, mat1234567_6, mat1234567_7, row1, row12, row123;

  matmul matmul_1 (
    .x_row_0(x_row_0), .x_row_1(x_row_1), .x_row_2(x_row_2), .x_row_3(x_row_3), .x_row_4(x_row_4),
    .x_row_5(x_row_5), .x_row_6(x_row_6), .x_row_7(x_row_7), .y_row_0(x_row_0), .y_row_1(x_row_1),
    .y_row_2(x_row_2), .y_row_3(x_row_3), .y_row_4(x_row_4), .y_row_5(x_row_5), .y_row_6(x_row_6),
    .y_row_7(x_row_7), .z_row_0(mat12_0), .z_row_1(mat12_1), .z_row_2(mat12_2), .z_row_3(mat12_3),
    .z_row_4(mat12_4), .z_row_5(mat12_5), .z_row_6(mat12_6), .z_row_7(mat12_7));
  matmul matmul_2 (
    .x_row_0(mat12_0), .x_row_1(mat12_1), .x_row_2(mat12_2), .x_row_3(mat12_3), .x_row_4(mat12_4),
    .x_row_5(mat12_5), .x_row_6(mat12_6), .x_row_7(mat12_7), .y_row_0(x_row_0), .y_row_1(x_row_1),
    .y_row_2(x_row_2), .y_row_3(x_row_3), .y_row_4(x_row_4), .y_row_5(x_row_5), .y_row_6(x_row_6),
    .y_row_7(x_row_7), .z_row_0(mat123_0), .z_row_1(mat123_1), .z_row_2(mat123_2), .z_row_3(mat123_3),
    .z_row_4(mat123_4), .z_row_5(mat123_5), .z_row_6(mat123_6), .z_row_7(mat123_7));
  matmul matmul_3 (
    .x_row_0(mat123_0), .x_row_1(mat123_1), .x_row_2(mat123_2), .x_row_3(mat123_3), .x_row_4(mat123_4),
    .x_row_5(mat123_5), .x_row_6(mat123_6), .x_row_7(mat123_7), .y_row_0(x_row_0), .y_row_1(x_row_1),
    .y_row_2(x_row_2), .y_row_3(x_row_3), .y_row_4(x_row_4), .y_row_5(x_row_5), .y_row_6(x_row_6),
    .y_row_7(x_row_7), .z_row_0(mat1234_0), .z_row_1(mat1234_1), .z_row_2(mat1234_2), .z_row_3(mat1234_3),
    .z_row_4(mat1234_4), .z_row_5(mat1234_5), .z_row_6(mat1234_6), .z_row_7(mat1234_7));
  matmul matmul_4 (
    .x_row_0(mat1234_0), .x_row_1(mat1234_1), .x_row_2(mat1234_2), .x_row_3(mat1234_3), .x_row_4(mat1234_4),
    .x_row_5(mat1234_5), .x_row_6(mat1234_6), .x_row_7(mat1234_7), .y_row_0(x_row_0), .y_row_1(x_row_1),
    .y_row_2(x_row_2), .y_row_3(x_row_3), .y_row_4(x_row_4), .y_row_5(x_row_5), .y_row_6(x_row_6),
    .y_row_7(x_row_7), .z_row_0(mat12345_0), .z_row_1(mat12345_1), .z_row_2(mat12345_2),
    .z_row_3(mat12345_3), .z_row_4(mat12345_4), .z_row_5(mat12345_5), .z_row_6(mat12345_6),
    .z_row_7(mat12345_7));
  matmul matmul_5 (
    .x_row_0(mat12345_0), .x_row_1(mat12345_1), .x_row_2(mat12345_2), .x_row_3(mat12345_3),
    .x_row_4(mat12345_4), .x_row_5(mat12345_5), .x_row_6(mat12345_6), .x_row_7(mat12345_7),
    .y_row_0(x_row_0), .y_row_1(x_row_1), .y_row_2(x_row_2), .y_row_3(x_row_3), .y_row_4(x_row_4),
    .y_row_5(x_row_5), .y_row_6(x_row_6), .y_row_7(x_row_7), .z_row_0(mat123456_0), .z_row_1(mat123456_1),
    .z_row_2(mat123456_2), .z_row_3(mat123456_3), .z_row_4(mat123456_4), .z_row_5(mat123456_5),
    .z_row_6(mat123456_6), .z_row_7(mat123456_7));
  matmul matmul_6 (
    .x_row_0(mat123456_0), .x_row_1(mat123456_1), .x_row_2(mat123456_2), .x_row_3(mat123456_3),
    .x_row_4(mat123456_4), .x_row_5(mat123456_5), .x_row_6(mat123456_6), .x_row_7(mat123456_7),
    .y_row_0(x_row_0), .y_row_1(x_row_1), .y_row_2(x_row_2), .y_row_3(x_row_3), .y_row_4(x_row_4),
    .y_row_5(x_row_5), .y_row_6(x_row_6), .y_row_7(x_row_7), .z_row_0(mat1234567_0), .z_row_1(mat1234567_1),
    .z_row_2(mat1234567_2), .z_row_3(mat1234567_3), .z_row_4(mat1234567_4), .z_row_5(mat1234567_5),
    .z_row_6(mat1234567_6), .z_row_7(mat1234567_7));
  DotMatrix #(.inputtype("row"), .matrixcols(8), .matrixrows(8)) dotmatrix_1 (
    .row0(x_row_0), .row1(x_row_1), .row2(x_row_2), .row3(x_row_3), .row4(x_row_4), .row5(x_row_5),
    .row6(x_row_6), .row7(x_row_7));
  Multiplexer #(.select(3), .width(8), .enable("false")) multiplexer_1 (
    .in0(x_row_0), .in1(x_row_1), .in2(x_row_2), .in3(x_row_3), .in4(x_row_4), .in5(x_row_5), .in6(x_row_6),
    .in7(x_row_7), .out(row1), .sel(from));
  Multiplexer #(.select(3), .width(8), .enable("false")) multiplexer_2 (
    .in0(mat12_0), .in1(mat12_1), .in2(mat12_2), .in3(mat12_3), .in4(mat12_4), .in5(mat12_5), .in6(mat12_6),
    .in7(mat12_7), .out(row12), .sel(from));
  Multiplexer #(.select(3), .width(8), .enable("false")) multiplexer_3 (
    .in0(mat123_0), .in1(mat123_1), .in2(mat123_2), .in3(mat123_3), .in4(mat123_4), .in5(mat123_5),
    .in6(mat123_6), .in7(mat123_7), .out(row123), .sel(from));
  Multiplexer #(.select(3), .width(8), .enable("false")) multiplexer_4 (
    .in0(mat1234_0), .in1(mat1234_1), .in2(mat1234_2), .in3(mat1234_3), .in4(mat1234_4), .in5(mat1234_5),
    .in6(mat1234_6), .in7(mat1234_7), .out({row477, row466, row455, row444, row433, row422, row411, row400}),
    .sel(from));
  Multiplexer #(.select(3), .width(8), .enable("false")) multiplexer_5 (
    .in0(mat12345_0), .in1(mat12345_1), .in2(mat12345_2), .in3(mat12345_3), .in4(mat12345_4),
    .in5(mat12345_5), .in6(mat12345_6), .in7(mat12345_7),
    .out({row577, row566, row555, row544, row533, row522, row511, row500}), .sel(from));
  Multiplexer #(.select(3), .width(8), .enable("false")) multiplexer_6 (
    .in0(mat123456_0), .in1(mat123456_1), .in2(mat123456_2), .in3(mat123456_3), .in4(mat123456_4),
    .in5(mat123456_5), .in6(mat123456_6), .in7(mat123456_7),
    .out({row677, row666, row655, row644, row633, row622, row611, row600}), .sel(from));
  Multiplexer #(.select(3), .width(8), .enable("false")) multiplexer_7 (
    .in0(mat1234567_0), .in1(mat1234567_1), .in2(mat1234567_2), .in3(mat1234567_3), .in4(mat1234567_4),
    .in5(mat1234567_5), .in6(mat1234567_6), .in7(mat1234567_7),
    .out({row777, row766, row755, row744, row733, row722, row711, row700}), .sel(from));
  Multiplexer #(.select(3), .enable("false")) multiplexer_8 (
    .in0(loop), .in1(ans1), .in2(ans12), .in3(ans123), .in4(ans1234), .in5(ans12345), .in6(ans123456),
    .in7(ans1234567), .out(path_exists), .sel(num_steps));
  Multiplexer #(.select(3), .enable("false")) multiplexer_9 (
    .in0(row1[7]), .in1(row1[6]), .in2(row1[5]), .in3(row1[4]), .in4(row1[3]), .in5(row1[2]), .in6(row1[1]),
    .in7(row1[0]), .out(ans1), .sel(to));
  Multiplexer #(.select(3), .enable("false")) multiplexer_10 (
    .in0(row12[7]), .in1(row12[6]), .in2(row12[5]), .in3(row12[4]), .in4(row12[3]), .in5(row12[2]),
    .in6(row12[1]), .in7(row12[0]), .out(ans12), .sel(to));
  Multiplexer #(.select(3), .enable("false")) multiplexer_11 (
    .in0(row123[7]), .in1(row123[6]), .in2(row123[5]), .in3(row123[4]), .in4(row123[3]), .in5(row123[2]),
    .in6(row123[1]), .in7(row123[0]), .out(ans123), .sel(to));
  Multiplexer #(.select(3), .enable("false")) multiplexer_12 (
    .in0(row477), .in1(row466), .in2(row455), .in3(row444), .in4(row433), .in5(row422), .in6(row411),
    .in7(row400), .out(ans1234), .sel(to));
  Multiplexer #(.select(3), .enable("false")) multiplexer_13 (
    .in0(row577), .in1(row566), .in2(row555), .in3(row544), .in4(row533), .in5(row522), .in6(row511),
    .in7(row500), .out(ans12345), .sel(to));
  Multiplexer #(.select(3), .enable("false")) multiplexer_14 (
    .in0(row677), .in1(row666), .in2(row655), .in3(row644), .in4(row633), .in5(row622), .in6(row611),
    .in7(row600), .out(ans123456), .sel(to));
  and and_1 (and_1_out, xnor_1_out, xnor_2_out);
  xnor xnor_1 (xnor_1_out, to[0], from[0]);
  Multiplexer #(.select(3), .enable("false")) multiplexer_15 (
    .in0(row777), .in1(row766), .in2(row755), .in3(row744), .in4(row733), .in5(row722), .in6(row711),
    .in7(row700), .out(ans1234567), .sel(to));
  and and_2 (loop, and_1_out, and_3_out);
  xnor xnor_2 (xnor_2_out, to[1], from[1]);
  and and_3 (and_3_out, xnor_2_out, xnor_3_out);
  xnor xnor_3 (xnor_3_out, to[2], from[2]);

  // Other names for the same wires on the sheet: from_0 = from[0]; from_1 = from[1]; from_2 = from[2];
  //   row1n[7:0] = {row1[0], row1[1], row1[2], row1[3], row1[4], row1[5], row1[6], row1[7]}; row177 = row1[7];
  //   row166 = row1[6]; row155 = row1[5]; row144 = row1[4]; row133 = row1[3]; row122 = row1[2]; row111 = row1[1];
  //   row100 = row1[0];
  //   row12n[7:0] = {row12[0], row12[1], row12[2], row12[3], row12[4], row12[5], row12[6], row12[7]};
  //   row277 = row12[7]; row266 = row12[6]; row255 = row12[5]; row244 = row12[4]; row233 = row12[3];
  //   row222 = row12[2]; row211 = row12[1]; row200 = row12[0];
  //   row123n[7:0] = {row123[0], row123[1], row123[2], row123[3], row123[4], row123[5], row123[6], row123[7]};
  //   row377 = row123[7]; row366 = row123[6]; row355 = row123[5]; row344 = row123[4]; row333 = row123[3];
  //   row322 = row123[2]; row311 = row123[1]; row300 = row123[0];
  //   row1234[7:0] = {row477, row466, row455, row444, row433, row422, row411, row400};
  //   row1234n[7:0] = {row400, row411, row422, row433, row444, row455, row466, row477};
  //   row12345[7:0] = {row577, row566, row555, row544, row533, row522, row511, row500};
  //   row12345n[7:0] = {row500, row511, row522, row533, row544, row555, row566, row577};
  //   row123456[7:0] = {row677, row666, row655, row644, row633, row622, row611, row600};
  //   row123456n[7:0] = {row600, row611, row622, row633, row644, row655, row666, row677};
  //   row1234567[7:0] = {row777, row766, row755, row744, row733, row722, row711, row700};
  //   row1234567n[7:0] = {row700, row711, row722, row733, row744, row755, row766, row777}; to_0 = to[0]; to_1 = to[1];
  //   to_2 = to[2]
endmodule

module atmost (
  input  [7:0] x_row_0,
  input  [7:0] x_row_1,
  input  [7:0] x_row_2,
  input  [7:0] x_row_3,
  input  [7:0] x_row_4,
  input  [7:0] x_row_5,
  input  [7:0] x_row_6,
  input  [7:0] x_row_7,
  input  [2:0] from,
  input  [2:0] to,
  input  [2:0] num_steps,
  output path_exists
);

  wire and_1_out, and_2_out, and_3_out, and_4_out, and_5_out, and_6_out, and_7_out, and_8_out, and_10_out,
       and_11_out, and_12_out, and_13_out, and_14_out, and_15_out, ans1, ans12, ans123, ans1234, ans12345,
       ans123456, ans1234567, loop, or_1_out, or_2_out, or_3_out, or_4_out, or_5_out, or_6_out, or_7_out,
       or_9_out, or_10_out, or_11_out, or_12_out, or_13_out, row400, row411, row422, row433, row444, row455,
       row466, row477, row500, row511, row522, row533, row544, row555, row566, row577, row600, row611,
       row622, row633, row644, row655, row666, row677, row700, row711, row722, row733, row744, row755,
       row766, row777, xnor_1_out, xnor_2_out, xnor_3_out;
  wire [7:0] mat12_0, mat12_1, mat12_2, mat12_3, mat12_4, mat12_5, mat12_6, mat12_7, mat123_0, mat123_1,
       mat123_2, mat123_3, mat123_4, mat123_5, mat123_6, mat123_7, mat1234_0, mat1234_1, mat1234_2,
       mat1234_3, mat1234_4, mat1234_5, mat1234_6, mat1234_7, mat12345_0, mat12345_1, mat12345_2, mat12345_3,
       mat12345_4, mat12345_5, mat12345_6, mat12345_7, mat123456_0, mat123456_1, mat123456_2, mat123456_3,
       mat123456_4, mat123456_5, mat123456_6, mat123456_7, mat1234567_0, mat1234567_1, mat1234567_2,
       mat1234567_3, mat1234567_4, mat1234567_5, mat1234567_6, mat1234567_7, row1, row12, row123;

  matmul matmul_1 (
    .x_row_0(x_row_0), .x_row_1(x_row_1), .x_row_2(x_row_2), .x_row_3(x_row_3), .x_row_4(x_row_4),
    .x_row_5(x_row_5), .x_row_6(x_row_6), .x_row_7(x_row_7), .y_row_0(x_row_0), .y_row_1(x_row_1),
    .y_row_2(x_row_2), .y_row_3(x_row_3), .y_row_4(x_row_4), .y_row_5(x_row_5), .y_row_6(x_row_6),
    .y_row_7(x_row_7), .z_row_0(mat12_0), .z_row_1(mat12_1), .z_row_2(mat12_2), .z_row_3(mat12_3),
    .z_row_4(mat12_4), .z_row_5(mat12_5), .z_row_6(mat12_6), .z_row_7(mat12_7));
  matmul matmul_2 (
    .x_row_0(mat12_0), .x_row_1(mat12_1), .x_row_2(mat12_2), .x_row_3(mat12_3), .x_row_4(mat12_4),
    .x_row_5(mat12_5), .x_row_6(mat12_6), .x_row_7(mat12_7), .y_row_0(x_row_0), .y_row_1(x_row_1),
    .y_row_2(x_row_2), .y_row_3(x_row_3), .y_row_4(x_row_4), .y_row_5(x_row_5), .y_row_6(x_row_6),
    .y_row_7(x_row_7), .z_row_0(mat123_0), .z_row_1(mat123_1), .z_row_2(mat123_2), .z_row_3(mat123_3),
    .z_row_4(mat123_4), .z_row_5(mat123_5), .z_row_6(mat123_6), .z_row_7(mat123_7));
  matmul matmul_3 (
    .x_row_0(mat123_0), .x_row_1(mat123_1), .x_row_2(mat123_2), .x_row_3(mat123_3), .x_row_4(mat123_4),
    .x_row_5(mat123_5), .x_row_6(mat123_6), .x_row_7(mat123_7), .y_row_0(x_row_0), .y_row_1(x_row_1),
    .y_row_2(x_row_2), .y_row_3(x_row_3), .y_row_4(x_row_4), .y_row_5(x_row_5), .y_row_6(x_row_6),
    .y_row_7(x_row_7), .z_row_0(mat1234_0), .z_row_1(mat1234_1), .z_row_2(mat1234_2), .z_row_3(mat1234_3),
    .z_row_4(mat1234_4), .z_row_5(mat1234_5), .z_row_6(mat1234_6), .z_row_7(mat1234_7));
  matmul matmul_4 (
    .x_row_0(mat1234_0), .x_row_1(mat1234_1), .x_row_2(mat1234_2), .x_row_3(mat1234_3), .x_row_4(mat1234_4),
    .x_row_5(mat1234_5), .x_row_6(mat1234_6), .x_row_7(mat1234_7), .y_row_0(x_row_0), .y_row_1(x_row_1),
    .y_row_2(x_row_2), .y_row_3(x_row_3), .y_row_4(x_row_4), .y_row_5(x_row_5), .y_row_6(x_row_6),
    .y_row_7(x_row_7), .z_row_0(mat12345_0), .z_row_1(mat12345_1), .z_row_2(mat12345_2),
    .z_row_3(mat12345_3), .z_row_4(mat12345_4), .z_row_5(mat12345_5), .z_row_6(mat12345_6),
    .z_row_7(mat12345_7));
  matmul matmul_5 (
    .x_row_0(mat12345_0), .x_row_1(mat12345_1), .x_row_2(mat12345_2), .x_row_3(mat12345_3),
    .x_row_4(mat12345_4), .x_row_5(mat12345_5), .x_row_6(mat12345_6), .x_row_7(mat12345_7),
    .y_row_0(x_row_0), .y_row_1(x_row_1), .y_row_2(x_row_2), .y_row_3(x_row_3), .y_row_4(x_row_4),
    .y_row_5(x_row_5), .y_row_6(x_row_6), .y_row_7(x_row_7), .z_row_0(mat123456_0), .z_row_1(mat123456_1),
    .z_row_2(mat123456_2), .z_row_3(mat123456_3), .z_row_4(mat123456_4), .z_row_5(mat123456_5),
    .z_row_6(mat123456_6), .z_row_7(mat123456_7));
  matmul matmul_6 (
    .x_row_0(mat123456_0), .x_row_1(mat123456_1), .x_row_2(mat123456_2), .x_row_3(mat123456_3),
    .x_row_4(mat123456_4), .x_row_5(mat123456_5), .x_row_6(mat123456_6), .x_row_7(mat123456_7),
    .y_row_0(x_row_0), .y_row_1(x_row_1), .y_row_2(x_row_2), .y_row_3(x_row_3), .y_row_4(x_row_4),
    .y_row_5(x_row_5), .y_row_6(x_row_6), .y_row_7(x_row_7), .z_row_0(mat1234567_0), .z_row_1(mat1234567_1),
    .z_row_2(mat1234567_2), .z_row_3(mat1234567_3), .z_row_4(mat1234567_4), .z_row_5(mat1234567_5),
    .z_row_6(mat1234567_6), .z_row_7(mat1234567_7));
  and and_1 (and_1_out, ans1, or_2_out);
  or or_1 (or_1_out, num_steps[0], num_steps[1]);
  or or_2 (or_2_out, or_1_out, or_3_out);
  or or_3 (or_3_out, num_steps[1], num_steps[2]);
  DotMatrix #(.inputtype("row"), .matrixcols(8), .matrixrows(8)) dotmatrix_1 (
    .row0(x_row_0), .row1(x_row_1), .row2(x_row_2), .row3(x_row_3), .row4(x_row_4), .row5(x_row_5),
    .row6(x_row_6), .row7(x_row_7));
  Multiplexer #(.select(3), .width(8), .enable("false")) multiplexer_1 (
    .in0(x_row_0), .in1(x_row_1), .in2(x_row_2), .in3(x_row_3), .in4(x_row_4), .in5(x_row_5), .in6(x_row_6),
    .in7(x_row_7), .out(row1), .sel(from));
  Multiplexer #(.select(3), .width(8), .enable("false")) multiplexer_2 (
    .in0(mat12_0), .in1(mat12_1), .in2(mat12_2), .in3(mat12_3), .in4(mat12_4), .in5(mat12_5), .in6(mat12_6),
    .in7(mat12_7), .out(row12), .sel(from));
  Multiplexer #(.select(3), .width(8), .enable("false")) multiplexer_3 (
    .in0(mat123_0), .in1(mat123_1), .in2(mat123_2), .in3(mat123_3), .in4(mat123_4), .in5(mat123_5),
    .in6(mat123_6), .in7(mat123_7), .out(row123), .sel(from));
  Multiplexer #(.select(3), .width(8), .enable("false")) multiplexer_4 (
    .in0(mat1234_0), .in1(mat1234_1), .in2(mat1234_2), .in3(mat1234_3), .in4(mat1234_4), .in5(mat1234_5),
    .in6(mat1234_6), .in7(mat1234_7), .out({row477, row466, row455, row444, row433, row422, row411, row400}),
    .sel(from));
  Multiplexer #(.select(3), .width(8), .enable("false")) multiplexer_5 (
    .in0(mat12345_0), .in1(mat12345_1), .in2(mat12345_2), .in3(mat12345_3), .in4(mat12345_4),
    .in5(mat12345_5), .in6(mat12345_6), .in7(mat12345_7),
    .out({row577, row566, row555, row544, row533, row522, row511, row500}), .sel(from));
  or or_4 (or_4_out, loop, and_1_out);
  and and_2 (and_2_out, ans12, or_7_out);
  Multiplexer #(.select(3), .width(8), .enable("false")) multiplexer_6 (
    .in0(mat123456_0), .in1(mat123456_1), .in2(mat123456_2), .in3(mat123456_3), .in4(mat123456_4),
    .in5(mat123456_5), .in6(mat123456_6), .in7(mat123456_7),
    .out({row677, row666, row655, row644, row633, row622, row611, row600}), .sel(from));
  Multiplexer #(.select(3), .width(8), .enable("false")) multiplexer_7 (
    .in0(mat1234567_0), .in1(mat1234567_1), .in2(mat1234567_2), .in3(mat1234567_3), .in4(mat1234567_4),
    .in5(mat1234567_5), .in6(mat1234567_6), .in7(mat1234567_7),
    .out({row777, row766, row755, row744, row733, row722, row711, row700}), .sel(from));
  or or_5 (or_5_out, or_4_out, or_6_out);
  or or_6 (or_6_out, and_2_out, and_3_out);
  or or_7 (or_7_out, num_steps[1], num_steps[2]);
  or or_8 (path_exists, or_5_out, or_10_out);
  Multiplexer #(.select(3), .enable("false")) multiplexer_8 (
    .in0(row1[7]), .in1(row1[6]), .in2(row1[5]), .in3(row1[4]), .in4(row1[3]), .in5(row1[2]), .in6(row1[1]),
    .in7(row1[0]), .out(ans1), .sel(to));
  Multiplexer #(.select(3), .enable("false")) multiplexer_9 (
    .in0(row12[7]), .in1(row12[6]), .in2(row12[5]), .in3(row12[4]), .in4(row12[3]), .in5(row12[2]),
    .in6(row12[1]), .in7(row12[0]), .out(ans12), .sel(to));
  Multiplexer #(.select(3), .enable("false")) multiplexer_10 (
    .in0(row123[7]), .in1(row123[6]), .in2(row123[5]), .in3(row123[4]), .in4(row123[3]), .in5(row123[2]),
    .in6(row123[1]), .in7(row123[0]), .out(ans123), .sel(to));
  and and_3 (and_3_out, ans123, or_9_out);
  Multiplexer #(.select(3), .enable("false")) multiplexer_11 (
    .in0(row477), .in1(row466), .in2(row455), .in3(row444), .in4(row433), .in5(row422), .in6(row411),
    .in7(row400), .out(ans1234), .sel(to));
  Multiplexer #(.select(3), .enable("false")) multiplexer_12 (
    .in0(row577), .in1(row566), .in2(row555), .in3(row544), .in4(row533), .in5(row522), .in6(row511),
    .in7(row500), .out(ans12345), .sel(to));
  Multiplexer #(.select(3), .enable("false")) multiplexer_13 (
    .in0(row677), .in1(row666), .in2(row655), .in3(row644), .in4(row633), .in5(row622), .in6(row611),
    .in7(row600), .out(ans123456), .sel(to));
  and and_4 (and_4_out, num_steps[1], num_steps[0]);
  Multiplexer #(.select(3), .enable("false")) multiplexer_14 (
    .in0(row777), .in1(row766), .in2(row755), .in3(row744), .in4(row733), .in5(row722), .in6(row711),
    .in7(row700), .out(ans1234567), .sel(to));
  or or_9 (or_9_out, and_4_out, num_steps[2]);
  and and_5 (and_5_out, ans1234, num_steps[2]);
  or or_10 (or_10_out, or_11_out, or_12_out);
  or or_11 (or_11_out, and_5_out, and_6_out);
  xnor xnor_1 (xnor_1_out, to[0], from[0]);
  and and_6 (and_6_out, ans12345, and_8_out);
  and and_7 (and_7_out, xnor_1_out, xnor_2_out);
  and and_8 (and_8_out, num_steps[2], or_13_out);
  and and_9 (loop, and_7_out, and_10_out);
  xnor xnor_2 (xnor_2_out, to[1], from[1]);
  or or_12 (or_12_out, and_11_out, and_12_out);
  or or_13 (or_13_out, num_steps[1], num_steps[0]);
  and and_10 (and_10_out, xnor_2_out, xnor_3_out);
  xnor xnor_3 (xnor_3_out, to[2], from[2]);
  and and_11 (and_11_out, ans123456, and_14_out);
  and and_12 (and_12_out, ans1234567, and_13_out);
  and and_13 (and_13_out, num_steps[2], and_15_out);
  and and_14 (and_14_out, num_steps[2], num_steps[1]);
  and and_15 (and_15_out, num_steps[1], num_steps[0]);

  // Other names for the same wires on the sheet: from_0 = from[0]; from_1 = from[1]; from_2 = from[2];
  //   num_step_0 = num_steps[0]; num_step_1 = num_steps[1]; num_step_2 = num_steps[2];
  //   row1n[7:0] = {row1[0], row1[1], row1[2], row1[3], row1[4], row1[5], row1[6], row1[7]}; row177 = row1[7];
  //   row166 = row1[6]; row155 = row1[5]; row144 = row1[4]; row133 = row1[3]; row122 = row1[2]; row111 = row1[1];
  //   row100 = row1[0];
  //   row12n[7:0] = {row12[0], row12[1], row12[2], row12[3], row12[4], row12[5], row12[6], row12[7]};
  //   row277 = row12[7]; row266 = row12[6]; row255 = row12[5]; row244 = row12[4]; row233 = row12[3];
  //   row222 = row12[2]; row211 = row12[1]; row200 = row12[0];
  //   row123n[7:0] = {row123[0], row123[1], row123[2], row123[3], row123[4], row123[5], row123[6], row123[7]};
  //   row377 = row123[7]; row366 = row123[6]; row355 = row123[5]; row344 = row123[4]; row333 = row123[3];
  //   row322 = row123[2]; row311 = row123[1]; row300 = row123[0];
  //   row1234[7:0] = {row477, row466, row455, row444, row433, row422, row411, row400};
  //   row1234n[7:0] = {row400, row411, row422, row433, row444, row455, row466, row477};
  //   row12345[7:0] = {row577, row566, row555, row544, row533, row522, row511, row500};
  //   row12345n[7:0] = {row500, row511, row522, row533, row544, row555, row566, row577};
  //   row123456[7:0] = {row677, row666, row655, row644, row633, row622, row611, row600};
  //   row123456n[7:0] = {row600, row611, row622, row633, row644, row655, row666, row677};
  //   row1234567[7:0] = {row777, row766, row755, row744, row733, row722, row711, row700};
  //   row1234567n[7:0] = {row700, row711, row722, row733, row744, row755, row766, row777}; to_0 = to[0]; to_1 = to[1];
  //   to_2 = to[2]
endmodule
